# Fritzing sketch FINAL-PROJECT-INDUCTANCE (saved by Fritzing 0.9.3b)
breadboards: 1

parts:
  Part1 = Arduino Mega ADK (Rev3)
  D1 = Rectifier Diode [part_number=1N4001 package="300 mil [THT]"]
  R1 = Resistor [tolerance=±5% resistance=150 package=THT]
  L1 = Inductor [package="400 mil [THT]"]
  C1 = Capacitor [package=cap-pth-small2]
  C2 = Capacitor [package=cap-pth-small2]
  LM339 = 556 [package=dil14]
  R2 = Resistor [tolerance=±5% resistance=330 package=THT]

nets:
  N1: Part1.GND, L1.pin_1, C1.1, C2.2, LM339.OUT, LM339.DIS2, R2.Pin_0
  N2: Part1.D9_PWM, R1.Pin_0
  N3: Part1.D8_PWM, LM339.TRIG2, R2.Pin_1
  N4: Part1.5V, LM339.RST2
  N5: D1.cathode, R1.Pin_1
  N6: D1.anode, L1.pin_0, C1.2, C2.1
